# Fritzing sketch invernadero (saved by Fritzing 0.9.3b)

parts:
  Part1 = Arduino Mega 2560 (Rev3)
  Raspberry_Pi_1 = Raspberry Pi 3 [part_number=RPI-3-V1.2]  # not connected
  RHT1 = Humidity and Temperature Sensor RHT03
  RHT2 = Humidity and Temperature Sensor RHT03
  RHT3 = Humidity and Temperature Sensor RHT03
  U1 = HIH-4030 [package=hih-4030]
  U2 = HIH-4030 [package=hih-4030]
  U3 = HIH-4030 [package=hih-4030]
  U4 = HIH-4030 [package=hih-4030]
  U5 = HIH-4030 [package=hih-4030]

nets:
  N1: Part1.A0, U1.OUT
  VCC: Part1.5V, RHT1.Vcc, RHT2.Vcc, RHT3.Vcc, U1.VCC, U2.VCC, U3.VCC, U4.VCC, U5.VCC
  GND: Part1.GND, RHT1.GND_1, RHT2.GND_1, RHT3.GND_1, U1.GND, U2.GND, U3.GND, U4.GND, U5.GND
  N2: Part1.D2_PWM, RHT1.Data-signal
  N3: Part1.D3_PWM, RHT2.Data-signal
  N4: Part1.D4_PWM, RHT3.Data-signal

notes:
  Conexión USB
